# Fritzing sketch hangboard (saved by Fritzing 0.9.4)

parts:
  MCU1 = Raspberry Pi Zero
  Bauteil1 = InvenSense MPU6050
  Bauteil2 = HX711 Weighing Sensor Module
  HC-SR04_Sensor_1 = HC-SR04 Ultrasonic Distance Sensor
  R1 = Resistor [tolerance=±5% resistance=330 package=THT]
  R2 = Resistor [tolerance=±5% resistance=100 package=THT]

nets:
  VCC: MCU1.pin_1, MCU1.pin_17, Bauteil1.VCC, Bauteil2.VCC
  N1: MCU1.pin_2, MCU1.pin_4, HC-SR04_Sensor_1.VCC
  N2: MCU1.pin_3, Bauteil1.SDA
  N3: MCU1.pin_5, Bauteil1.SCL
  GND: MCU1.pin_6, MCU1.pin_9, MCU1.pin_25, MCU1.pin_30, MCU1.pin_34, MCU1.pin_39, Bauteil1.GND, Bauteil2.GND, HC-SR04_Sensor_1.GND, R2.Pin_1
  N4: MCU1.pin_11, Bauteil2.CK/TX
  N5: MCU1.pin_12, HC-SR04_Sensor_1.TRIG
  N6: MCU1.pin_13, Bauteil2.DO/RX
  N7: MCU1.pin_18, R1.Pin_1, R2.Pin_0
  N8: HC-SR04_Sensor_1.ECHO, R1.Pin_0
